# Fritzing sketch Untitled Sketch (saved by Fritzing 0.9.3b)
circuit board: 7.89742cm x 2.81763cm
breadboards: 1

parts:
  U1 = ESP8266 WiFi Module [part_number=ESP8266]
  LOUT1 = female pin header, 3 pins [form="♀ (female)"]
  C3 = Ceramic Capacitor [capacitance=100nF package="100 mil [THT, multilayer]"]
  D1 = Rectifier Diode [part_number=1N4001 package="300 mil [THT]"]
  R1 = Resistor [tolerance=±5% resistance=220 package=THT]
  R2 = Resistor [tolerance=±5% resistance=220 package=THT]
  R3 = Resistor [tolerance=±5% resistance=220 package=THT]
  R4 = Resistor [tolerance=±5% resistance=220 package=THT]
  COM = female pin header, 3 pins [form="♀ (female)"]
  JPR1 = female pin header, 2 pins [form="♀ (female)"]
  LOUT2 = female pin header, 3 pins [form="♀ (female)"]
  GPIO = female pin header, 6 pins [form="♀ (female)"]
  C2 = Ceramic Capacitor [capacitance=100nF package="200 mil [THT, multilayer]"]
  IC1 = Voltage Regulator LM1117 [package=sot223]
  C5 = Ceramic Capacitor [capacitance=100nF package="100 mil [THT, multilayer]"]
  IC2 = IC, DIP package, 14 pins [chip_label=74AHCT125 part_number=74AHCT125]
  R5 = Resistor [tolerance=±5% resistance=220 package=THT]
  R6 = Resistor [tolerance=±5% resistance=220 package=THT]
  C6 = Electrolytic Capacitor [capacitance=0.1mF package="100 mil [THT, electrolytic]"]
  C1 = Electrolytic Capacitor [capacitance=0.1mF package="100 mil [THT, electrolytic]"]
  PWR = screw terminal, 2 pins

nets:
  N1: U1.RXD, COM.pin1
  3V3: U1.VCC, C3.0, R2.Pin_0, R4.Pin_0, GPIO.pin6, IC1.OUT, C5.0
  N2: U1.GPIO_0, JPR1.pin2
  N3: U1.GPIO_2, R4.Pin_1
  N4: U1.CH_PD, R2.Pin_1
  GND: U1.GND, LOUT1.pin3, C3.1, R3.Pin_0, COM.pin3, JPR1.pin1, LOUT2.pin3, GPIO.pin1, C2.1, IC1.ADJ, C5.1, IC2.pin7, IC2.pin10, IC2.pin13, C6.-, C1.-, PWR.pin1
  N5: U1.TXD, COM.pin2
  N6: U1.GPIO_15, R3.Pin_1
  LED1: U1.GPIO_4, IC2.pin12
  LED2: U1.GPIO_5, IC2.pin9
  N7: U1.ADC_0, GPIO.pin2
  N8: U1.GPIO_16, R1.Pin_1
  N9: U1.GPIO_14, GPIO.pin3
  N10: U1.GPIO_12, GPIO.pin4
  N11: U1.GPIO_13, GPIO.pin5
  N12: U1.REST, R1.Pin_0
  5V: LOUT1.pin1, D1.anode, LOUT2.pin1, IC2.pin14, C6.+, C1.+, PWR.pin2
  N13: LOUT1.pin2, R6.Pin_1
  N14: D1.cathode, C2.0, IC1.IN
  N15: LOUT2.pin2, R5.Pin_1
  LDATA2: IC2.pin8, R5.Pin_0
  LDATA1: IC2.pin11, R6.Pin_0

notes:
  GND
  Tx
  Rx
